# Fritzing sketch sound (saved by Fritzing 0.9.4)
breadboards: 1

parts:
  Mic1 = KY-038
  Part1 = Arduino Uno (Rev3) - ICSP
  LED1 = smd LED [color="Red (633nm)" package="0805 [SMD]"]
  R1 = Resistor [tolerance=±5% resistance=220 package="1206 [SMD]"]

nets:
  N1: Mic1.pin2, Part1.GND, R1.Pin_0
  N2: Mic1.pin3, Part1.5V
  N3: Mic1.pin4, Part1.D2
  N4: Part1.D3_PWM, LED1.anode
  N5: LED1.cathode, R1.Pin_1

custom parts:
  KY-038: ky-038 Microphone sound sensor module
