# Fritzing sketch pir-relay (saved by Fritzing 0.9.4)
breadboards: 1

parts:
  Part1 = Arduino Uno (Rev3) - ICSP
  Part2 = KY-019 5V Relay Module [package="Breakout board"]
  PIR1 = PIR sensor
  LED1 = LEDs [package=led10mm]

nets:
  N1: Part1.D6_PWM, Part2.S
  N2: Part1.D7, PIR1.SIG
  5V: Part1.5V, Part2.+, PIR1.VDD
  GND: Part1.GND, Part2.-, PIR1.GND
  N3: Part2.NO, LED1.C

custom parts:
  KY-019 5V Relay Module: KY-019 5V Relay module, used to control AC circuits.
  LEDs: LEDs Standard schematic elements and footprints for 5mm, 3mm, 1206, and 0603 sized LEDs. 5mm - Spark Fun Electronics SKU : COM-00529 (and others)
