# Fritzing sketch radar (saved by Fritzing 0.9.4)
breadboards: 1

parts:
  M1 = Dagu DGServo 9g (Top view) [part_number=RS001B]
  HC-SR04_Sensor_1 = HC-SR04 Ultrasonic Distance Sensor
  Part1 = Arduino Uno (Rev3) - ICSP

nets:
  GND: M1.gnd, HC-SR04_Sensor_1.GND, Part1.GND
  VCC: M1.vcc, HC-SR04_Sensor_1.VCC, Part1.5V
  N1: M1.pulse, Part1.D4
  N2: HC-SR04_Sensor_1.TRIG, Part1.D3_PWM
  N3: HC-SR04_Sensor_1.ECHO, Part1.D2
