# Fritzing sketch rfid (saved by Fritzing 0.9.4)
breadboards: 1

parts:
  Part1 = Arduino Uno (Rev3) - ICSP
  M1 = Dagu DGServo 9g (Top view) [part_number=RS001B]
  Part2 = LCD1602-I2C
  Part3 = RFID-RC522-v2

nets:
  N1: Part1.A4/SDA, Part2.SDA
  N2: Part1.A5/SCL, Part2.SCL
  N3: Part1.D9_PWM, Part3.RST
  N4: Part1.D10_PWM/SS, Part3.SDA
  N5: Part1.D11_PWM/MOSI, Part3.MOSI
  N6: Part1.D12/MISO, Part3.MISO
  N7: Part1.D13/SCK, Part3.SCK
  N8: Part1.D4, M1.pulse
  3V3: Part1.3V3, Part3.3.3V
  VCC: Part1.5V, M1.vcc, Part2.VCC
  GND: Part1.GND, M1.gnd, Part2.GND, Part3.GND

custom parts:
  LCD1602-I2C: A standard character display, usually with 2x16 characters. Comes in many colors with LCM1602 IIC attached.
  RFID-RC522-v2: A simple China made RFID-RC522 Reader; do check the pin labels, as this is a MFRC522 based clone.
