# Fritzing sketch level (saved by Fritzing 0.9.4)
breadboards: 1

parts:
  Part1 = LCD1602-I2C
  Part2 = Color Sensor Breakout ADJD-S311  # not connected
  Part3 = Arduino Uno (Rev3) - ICSP
  R1 = Resistor [tolerance=±5% resistance=220 package=THT]
  R2 = Resistor [tolerance=±5% resistance=220 package=THT]

nets:
  GND: Part1.GND, Part3.GND
  VCC: Part1.VCC, Part3.5V
  N1: Part1.SDA, Part3.A4/SDA, R1.Pin_1
  N2: Part1.SCL, Part3.A5/SCL, R2.Pin_1
  N3: Part3.3V3, R1.Pin_0, R2.Pin_0

custom parts:
  LCD1602-I2C: A standard character display, usually with 2x16 characters. Comes in many colors with LCM1602 IIC attached.
